// Logisim project BASIC GATES.circ as structural Verilog: 1 circuit, main circuit main
module main (
  input  A,
  input  A_2,
  input  B_plus,
  input  A_3,
  input  B,
  input  in_6,
  input  in_7,
  input  A_4,
  input  B_2,
  input  in_10,
  input  in_11,
  input  A_5,
  input  B_3,
  output Q,
  output out_15,
  output Q_A_B,
  output out_17,
  output Q_A_B_2,
  output out_19,
  output out_20
);

  not not_1 (Q, A_2);
  and and_1 (Q_A_B, A_3, B);
  or or_1 (Q_A_B_2, A_4, B_2);
  nand nand_1 (out_20, A_5, B_3);
  or or_2 (out_15, A, B_plus);
  xor xor_1 (out_17, in_6, in_7);
  xnor xnor_1 (out_19, in_10, in_11);

  // Notes on the sheet:
  //   NOT GATE
  //   AND GATE
  //   OR GATE
  //   NAND GATE
  //   =A.B
  //   NOR GATE
  //   XOR GATE
  //   XNOR GATE
endmodule
