// Logisim project comparator.circ as structural Verilog: 1 circuit, main circuit main
module main (
  input  [3:0] in_1,
  input  [3:0] in_2
);

  wire comparator_1_eq, comparator_1_gt, comparator_1_lt;

  Comparator #(.width(4)) comparator_1 (
    .a(in_1), .b(in_2), .gt(comparator_1_gt), .eq(comparator_1_eq), .lt(comparator_1_lt));
  DotMatrix #(.matrixcols(3), .matrixrows(1)) dotmatrix_1 (
    .col0(comparator_1_gt), .col1(comparator_1_eq), .col2(comparator_1_lt));
endmodule
